// Logisim project DLD Project(Two-Way Traffic Lights)(1912461).circ as structural Verilog: 1 circuit, main circuit main
module main (
);

  wire and_1_out, and_2_out, and_3_out, and_4_out, and_5_out, and_6_out, and_7_out, and_8_out, and_9_out,
       and_10_out, and_11_out, and_12_out, clock_1_out, or_1_out, or_2_out, or_3_out, or_4_out, or_5_out,
       T0_q, T0_qn, T1_q, T1_qn, T2_q, T2_qn;

  Clock clock_1 (.out(clock_1_out));
  or or_1 (or_1_out, T2_qn, T1_qn, T0_q);
  and and_1 (and_1_out, T2_qn, T0_q);
  and and_2 (and_2_out, T1_q, T2_q);
  and and_3 (and_3_out, T0_q, T2_q);
  and and_4 (and_4_out, T2_q, T1_q);
  and and_5 (and_5_out, T0_q, T1_q);
  T_Flip_Flop T0 (.clk(clock_1_out), .T(or_1_out), .Q(T0_q), .Qn(T0_qn));  // open: preset, reset, en
  or or_2 (or_2_out, and_1_out, and_2_out);
  T_Flip_Flop T1 (.clk(clock_1_out), .T(or_2_out), .Q(T1_q), .Qn(T1_qn));  // open: preset, reset, en
  or or_3 (or_3_out, and_3_out, and_4_out, and_5_out);
  T_Flip_Flop T2 (.clk(clock_1_out), .T(or_3_out), .Q(T2_q), .Qn(T2_qn));  // open: preset, reset, en
  and and_6 (and_6_out, T1_q, T2_q);
  and and_7 (and_7_out, T2_qn, T1_qn, T0_qn);
  and and_8 (and_8_out, T2_qn, T1_q, T0_q);
  or or_4 (or_4_out, T2_qn, and_6_out);
  and and_9 (and_9_out, T2_q, T1_qn, T0_q);
  and and_10 (and_10_out, T2_q, T1_qn, T0_qn);
  LED R1 (.in(or_4_out));
  LED Y1 (.in(and_9_out));
  LED G1 (.in(and_10_out));
  LED R2 (.in(or_5_out));
  or or_5 (or_5_out, and_7_out, and_8_out, T2_q);
  and and_11 (and_11_out, T2_qn, T1_q, T0_qn);
  LED Y2 (.in(and_11_out));
  LED G2 (.in(and_12_out));
  and and_12 (and_12_out, T2_qn, T1_qn, T0_q);
endmodule
